// Logisim project 4bit_8word_Reg-enirris.circ as structural Verilog: 4 circuits, main circuit main
module main (
  input  In_0,
  input  In_1,
  input  In_2,
  input  In_3,
  input  Clock_input,
  input  A0,
  input  A1,
  input  A2,
  input  WE,
  output OUT_0,
  output OUT_1,
  output OUT_2,
  output OUT_3
);

  wire n38decoder_1_out_5, n38decoder_1_out_6, n38decoder_1_out_7, n38decoder_1_out_8, n38decoder_1_out_9,
       n38decoder_1_out_10, n38decoder_1_out_11, n38decoder_1_out_12;
  wire [3:0] n4bitregister_1_out_7, n4bitregister_2_out_7, n4bitregister_3_out_7, n4bitregister_4_out_7,
       n4bitregister_5_out_7, n4bitregister_6_out_7, n4bitregister_7_out_7, n4bitregister_8_out_7;

  _38Decoder u_38decoder_1 (
    .in_1(A0), .in_2(A1), .in_3(A2), .in_4(WE), .out_5(n38decoder_1_out_5), .out_6(n38decoder_1_out_6),
    .out_7(n38decoder_1_out_7), .out_8(n38decoder_1_out_8), .out_9(n38decoder_1_out_9),
    .out_10(n38decoder_1_out_10), .out_11(n38decoder_1_out_11), .out_12(n38decoder_1_out_12));
  _4BitRegister u_4bitregister_1 (
    .in_1(In_0), .in_2(In_1), .in_3(In_2), .in_4(In_3), .in_5(Clock_input), .in_6(n38decoder_1_out_5),
    .out_7(n4bitregister_1_out_7[0]), .out_8(n4bitregister_1_out_7[1]), .out_9(n4bitregister_1_out_7[2]),
    .out_10(n4bitregister_1_out_7[3]));
  _4BitRegister u_4bitregister_2 (
    .in_1(In_0), .in_2(In_1), .in_3(In_2), .in_4(In_3), .in_5(Clock_input), .in_6(n38decoder_1_out_7),
    .out_7(n4bitregister_2_out_7[0]), .out_8(n4bitregister_2_out_7[1]), .out_9(n4bitregister_2_out_7[2]),
    .out_10(n4bitregister_2_out_7[3]));
  _4BitRegister u_4bitregister_3 (
    .in_1(In_0), .in_2(In_1), .in_3(In_2), .in_4(In_3), .in_5(Clock_input), .in_6(n38decoder_1_out_9),
    .out_7(n4bitregister_3_out_7[0]), .out_8(n4bitregister_3_out_7[1]), .out_9(n4bitregister_3_out_7[2]),
    .out_10(n4bitregister_3_out_7[3]));
  _4BitRegister u_4bitregister_4 (
    .in_1(In_0), .in_2(In_1), .in_3(In_2), .in_4(In_3), .in_5(Clock_input), .in_6(n38decoder_1_out_11),
    .out_7(n4bitregister_4_out_7[0]), .out_8(n4bitregister_4_out_7[1]), .out_9(n4bitregister_4_out_7[2]),
    .out_10(n4bitregister_4_out_7[3]));
  _4BitRegister u_4bitregister_5 (
    .in_1(In_0), .in_2(In_1), .in_3(In_2), .in_4(In_3), .in_5(Clock_input), .in_6(n38decoder_1_out_6),
    .out_7(n4bitregister_5_out_7[0]), .out_8(n4bitregister_5_out_7[1]), .out_9(n4bitregister_5_out_7[2]),
    .out_10(n4bitregister_5_out_7[3]));
  _4BitRegister u_4bitregister_6 (
    .in_1(In_0), .in_2(In_1), .in_3(In_2), .in_4(In_3), .in_5(Clock_input), .in_6(n38decoder_1_out_8),
    .out_7(n4bitregister_6_out_7[0]), .out_8(n4bitregister_6_out_7[1]), .out_9(n4bitregister_6_out_7[2]),
    .out_10(n4bitregister_6_out_7[3]));
  _4BitRegister u_4bitregister_7 (
    .in_1(In_0), .in_2(In_1), .in_3(In_2), .in_4(In_3), .in_5(Clock_input), .in_6(n38decoder_1_out_10),
    .out_7(n4bitregister_7_out_7[0]), .out_8(n4bitregister_7_out_7[1]), .out_9(n4bitregister_7_out_7[2]),
    .out_10(n4bitregister_7_out_7[3]));
  _4BitRegister u_4bitregister_8 (
    .in_1(In_0), .in_2(In_1), .in_3(In_2), .in_4(In_3), .in_5(Clock_input), .in_6(n38decoder_1_out_12),
    .out_7(n4bitregister_8_out_7[0]), .out_8(n4bitregister_8_out_7[1]), .out_9(n4bitregister_8_out_7[2]),
    .out_10(n4bitregister_8_out_7[3]));
  Multiplexer #(.select(3), .width(4), .enable("false")) multiplexer_1 (
    .in0(n4bitregister_1_out_7), .in1(n4bitregister_5_out_7), .in2(n4bitregister_2_out_7),
    .in3(n4bitregister_6_out_7), .in4(n4bitregister_3_out_7), .in5(n4bitregister_7_out_7),
    .in6(n4bitregister_4_out_7), .in7(n4bitregister_8_out_7), .out({OUT_3, OUT_2, OUT_1, OUT_0}),
    .sel({A2, A1, A0}));
endmodule

module _38Decoder (
  input  in_1,
  input  in_2,
  input  in_3,
  input  in_4,
  output out_5,
  output out_6,
  output out_7,
  output out_8,
  output out_9,
  output out_10,
  output out_11,
  output out_12
);

  wire not_1_out, not_2_out, not_3_out;

  not not_1 (not_1_out, in_1);
  not not_2 (not_2_out, in_2);
  not not_3 (not_3_out, in_3);
  and and_1 (out_5, not_1_out, not_2_out, not_3_out, in_4);
  and and_2 (out_6, in_1, not_2_out, not_3_out, in_4);
  and and_3 (out_7, not_1_out, in_2, not_3_out, in_4);
  and and_4 (out_8, in_1, in_2, not_3_out, in_4);
  and and_5 (out_9, not_1_out, not_2_out, in_3, in_4);
  and and_6 (out_10, in_1, not_2_out, in_3, in_4);
  and and_7 (out_11, not_1_out, in_2, in_3, in_4);
  and and_8 (out_12, in_1, in_2, in_3, in_4);
endmodule

module _1BitRegister (
  input  in_1,
  input  in_2,
  input  in_3,
  output out_4
);

  wire multiplexer_1_out;

  Multiplexer #(.enable("false")) multiplexer_1 (.in0(out_4), .in1(in_2), .out(multiplexer_1_out), .sel(in_3));
  D_Flip_Flop d_ff_1 (.clk(in_1), .D(multiplexer_1_out), .Q(out_4));  // open: Qn, preset, en, reset
endmodule

module _4BitRegister (
  input  in_1,
  input  in_2,
  input  in_3,
  input  in_4,
  input  in_5,
  input  in_6,
  output out_7,
  output out_8,
  output out_9,
  output out_10
);

  _1BitRegister u_1bitregister_1 (.in_1(in_5), .in_2(in_1), .in_3(in_6), .out_4(out_7));
  _1BitRegister u_1bitregister_2 (.in_1(in_5), .in_2(in_2), .in_3(in_6), .out_4(out_8));
  _1BitRegister u_1bitregister_3 (.in_1(in_5), .in_2(in_3), .in_3(in_6), .out_4(out_9));
  _1BitRegister u_1bitregister_4 (.in_1(in_5), .in_2(in_4), .in_3(in_6), .out_4(out_10));
endmodule
