// Logisim project 4bit_ALU-enirris.circ as structural Verilog: 9 circuits, main circuit main
module main (
  input  A0,
  input  A1,
  input  A2,
  input  A3,
  input  B0,
  input  B1,
  input  B2,
  input  B3,
  input  S0,
  input  S1,
  output OUT_0,
  output OUT_1,
  output OUT_2,
  output OUT_3
);

  wire bit_wise_and_1_o0, bit_wise_and_1_o1, bit_wise_and_1_o2, bit_wise_and_1_o3, bit_wise_or_1_o0,
       bit_wise_or_1_o1, bit_wise_or_1_o2, bit_wise_or_1_o3, bit_wise_xor_1_o0, bit_wise_xor_1_o1,
       bit_wise_xor_1_o2, bit_wise_xor_1_o3, n4bitadder_1_out_0, n4bitadder_1_out_1, n4bitadder_1_out_2,
       n4bitadder_1_out_3;

  _4BitAdder u_4bitadder_1 (
    .A0(A0), .A1(A1), .A2(A2), .A3(A3), .B0(B0), .B1(B1), .B2(B2), .B3(B3), .OUT_0(n4bitadder_1_out_0),
    .OUT_1(n4bitadder_1_out_1), .OUT_2(n4bitadder_1_out_2), .OUT_3(n4bitadder_1_out_3));
  bit_wise_AND bit_wise_and_1 (
    .A0(A0), .A1(A1), .A2(A2), .A3(A3), .B0(B0), .B1(B1), .B2(B2), .B3(B3), .O0(bit_wise_and_1_o0),
    .O1(bit_wise_and_1_o1), .O2(bit_wise_and_1_o2), .O3(bit_wise_and_1_o3));
  bit_wise_OR bit_wise_or_1 (
    .A0(A0), .A1(A1), .A2(A2), .A3(A3), .B0(B0), .B1(B1), .B2(B2), .B3(B3), .O0(bit_wise_or_1_o0),
    .O1(bit_wise_or_1_o1), .O2(bit_wise_or_1_o2), .O3(bit_wise_or_1_o3));
  bit_wise_XOR bit_wise_xor_1 (
    .A0(A0), .A1(A1), .A2(A2), .A3(A3), .B0(B0), .B1(B1), .B2(B2), .B3(B3), .O0(bit_wise_xor_1_o0),
    .O1(bit_wise_xor_1_o1), .O2(bit_wise_xor_1_o2), .O3(bit_wise_xor_1_o3));
  Four4_1_MUX four4_1_mux_1 (
    .A0_3(n4bitadder_1_out_0), .in_2(n4bitadder_1_out_1), .in_3(n4bitadder_1_out_2),
    .in_4(n4bitadder_1_out_3), .B0_3(bit_wise_and_1_o0), .in_6(bit_wise_and_1_o1), .in_7(bit_wise_and_1_o2),
    .in_8(bit_wise_and_1_o3), .C0_3(bit_wise_or_1_o0), .in_10(bit_wise_or_1_o1), .in_11(bit_wise_or_1_o2),
    .in_12(bit_wise_or_1_o3), .D0_3(bit_wise_xor_1_o0), .in_14(bit_wise_xor_1_o1), .in_15(bit_wise_xor_1_o2),
    .in_16(bit_wise_xor_1_o3), .S1(S0), .S0(S1), .out_19(OUT_0), .out_20(OUT_1), .out_21(OUT_2),
    .out_22(OUT_3));

  // Notes on the sheet:
  //   Inputs
  //   ADD
  //   AND
  //   OR
  //   XOR
  //   Selectors
  //   4:1 MUX
  //   Outputs
endmodule

module fullAdder1Bit (
  input  A,
  input  B,
  input  C,
  output S,
  output C_2
);

  wire and_1_out, and_2_out, and_3_out;

  and and_1 (and_1_out, A, B);
  and and_2 (and_2_out, B, C);
  and and_3 (and_3_out, A, C);
  xor xor_1 (S, A, B, C);
  or or_1 (C_2, and_1_out, and_2_out, and_3_out);

  // Notes on the sheet:
  //   FullAdder1Bit
endmodule

module _4BitAdder (
  input  A0,
  input  A1,
  input  A2,
  input  A3,
  input  B0,
  input  B1,
  input  B2,
  input  B3,
  output OUT_0,
  output OUT_1,
  output OUT_2,
  output OUT_3
);

  wire fulladder1bit_1_c_2, fulladder1bit_2_c_2, fulladder1bit_3_c_2, fulladder1bit_4_c_2;

  fullAdder1Bit fulladder1bit_1 (.A(A0), .B(B0), .C(1'b0), .S(OUT_0), .C_2(fulladder1bit_1_c_2));
  fullAdder1Bit fulladder1bit_2 (.A(A1), .B(B1), .C(fulladder1bit_1_c_2), .S(OUT_1), .C_2(fulladder1bit_2_c_2));
  fullAdder1Bit fulladder1bit_3 (.A(A2), .B(B2), .C(fulladder1bit_2_c_2), .S(OUT_2), .C_2(fulladder1bit_3_c_2));
  fullAdder1Bit fulladder1bit_4 (.A(A3), .B(B3), .C(fulladder1bit_3_c_2), .S(OUT_3), .C_2(fulladder1bit_4_c_2));

  // Notes on the sheet:
  //   C
  //   C
endmodule

module bit_wise_AND (
  input  A0,
  input  A1,
  input  A2,
  input  A3,
  input  B0,
  input  B1,
  input  B2,
  input  B3,
  output O0,
  output O1,
  output O2,
  output O3
);

  and and_1 (O0, A0, B0);
  and and_2 (O1, A1, B1);
  and and_3 (O2, A2, B2);
  and and_4 (O3, A3, B3);
endmodule

module bit_wise_OR (
  input  A0,
  input  A1,
  input  A2,
  input  A3,
  input  B0,
  input  B1,
  input  B2,
  input  B3,
  output O0,
  output O1,
  output O2,
  output O3
);

  or or_1 (O0, A0, B0);
  or or_2 (O1, A1, B1);
  or or_3 (O2, A2, B2);
  or or_4 (O3, A3, B3);
endmodule

module bit_wise_XOR (
  input  A0,
  input  A1,
  input  A2,
  input  A3,
  input  B0,
  input  B1,
  input  B2,
  input  B3,
  output O0,
  output O1,
  output O2,
  output O3
);

  xor xor_1 (O0, A0, B0);
  xor xor_2 (O1, A1, B1);
  xor xor_3 (O2, A2, B2);
  xor xor_4 (O3, A3, B3);
endmodule

module Four4_1_MUX (
  input  A0_3,
  input  in_2,
  input  in_3,
  input  in_4,
  input  B0_3,
  input  in_6,
  input  in_7,
  input  in_8,
  input  C0_3,
  input  in_10,
  input  in_11,
  input  in_12,
  input  D0_3,
  input  in_14,
  input  in_15,
  input  in_16,
  input  S1,
  input  S0,
  output out_19,
  output out_20,
  output out_21,
  output out_22
);

  _4_1_MUX u_4_1_mux_1 (.A(A0_3), .B(B0_3), .C(C0_3), .D(D0_3), .S1(S1), .S0(S0), .F(out_19));
  _4_1_MUX u_4_1_mux_2 (.A(in_2), .B(in_6), .C(in_10), .D(in_14), .S1(S1), .S0(S0), .F(out_20));
  _4_1_MUX u_4_1_mux_3 (.A(in_3), .B(in_7), .C(in_11), .D(in_15), .S1(S1), .S0(S0), .F(out_21));
  _4_1_MUX u_4_1_mux_4 (.A(in_4), .B(in_8), .C(in_12), .D(in_16), .S1(S1), .S0(S0), .F(out_22));
endmodule

module _4_1_MUX (
  input  A,
  input  B,
  input  C,
  input  D,
  input  S1,
  input  S0,
  output F
);

  wire multiplexer_1_out, multiplexer_2_out;

  Multiplexer #(.enable("false")) multiplexer_1 (.in0(A), .in1(B), .out(multiplexer_1_out), .sel(S1));
  Multiplexer #(.enable("false")) multiplexer_2 (.in0(C), .in1(D), .out(multiplexer_2_out), .sel(S1));
  Multiplexer #(.enable("false")) multiplexer_3 (.in0(multiplexer_1_out), .in1(multiplexer_2_out), .out(F), .sel(S0));
endmodule

module _2_1_MUX (
  input  A,
  input  B,
  input  S,
  output out_4
);

  wire and_1_out, and_2_out, not_1_out;

  not not_1 (not_1_out, S);
  and and_1 (and_1_out, A, not_1_out);
  and and_2 (and_2_out, B, S);
  or or_1 (out_4, and_1_out, and_2_out);
endmodule
